# Fritzing sketch Flaschenfueller1 (saved by Fritzing 0.9.3b)

parts:
  Bauteil2 = Arduino Uno (Rev3) - ICSP
  Bauteil3 = LCD Keypad Shield
  U1 = Module 4 Relais 5V [package="Module 4 Relais 5V"]
  JACK1 = 2.1mm Barrel Jack with Terminal Block
  JACK2 = 2.1mm Barrel Jack with Terminal Block

nets:
  N1: Bauteil2.GND, JACK2.NEG
  N2: Bauteil2.VIN, JACK2.POS
  N3: Bauteil3.D11_MOSI, U1.IN3
  N4: Bauteil3.D12_MISO, U1.IN2
  N5: Bauteil3.D13_SCK, U1.IN1
  +5V: Bauteil3.+5V, U1.VCC
  N6: U1.GND, JACK1.NEG
  N7: U1.JD-VCC, JACK1.POS

notes:
  Füllstandskontakt
  12V

custom parts:
  LCD Keypad Shield: It consists of a 1602 white character blue backlight LCD. The keypad consists of 5 keys — select, up, right, down and left. To save the digital IO pins, the keypad interface uses only one ADC channel. The key value is read through a 5 stage voltage divider.
  Module 4 Relais 5V: Module 4 Relais 5V 4x SPD-06VDC-SD-C
